# Fritzing sketch Medicine-reminder (saved by Fritzing 0.9.3b)
breadboards: 1

parts:
  S1 = Pushbutton [package="[THT]"]
  Part1 = Arduino Nano (Rev3.0)  # not connected
  Part2 = Arduino Uno (Rev3)
  ZS-042_RTC1 = ZS-042 RTC Module
  R1 = Resistor [tolerance=±1% resistance=10k package=THT]
  R2 = Resistor [tolerance=±1% resistance=150 package=THT]
  R3 = Resistor [tolerance=±1% resistance=150 package=THT]
  R4 = Resistor [tolerance=±1% resistance=120 package=THT]
  LED1 = RGB LED - (4 legs) [package="5 mm [THT]"]  # not connected

nets:
  5V: S1.Pin_1, S1.Pin_2, Part2.5V, ZS-042_RTC1.VCC
  N1: S1.Pin_3, S1.Pin_4, Part2.D8, R1.Pin_1
  N2: Part2.D9_PWM, R3.Pin_1
  N3: Part2.D10_PWM/SS, R2.Pin_1
  N4: Part2.D11_PWM/MOSI, R4.Pin_1
  N5: Part2.A4/SDA, ZS-042_RTC1.SDA
  N6: Part2.A5/SCL, ZS-042_RTC1.SCL
  GND: Part2.GND, ZS-042_RTC1.GND, R1.Pin_0
