# Fritzing sketch Medicine-reminder-Uno (saved by Fritzing 0.9.3b)
breadboards: 1

parts:
  S1 = Pushbutton [package="[THT]"]
  Part2 = Arduino Uno (Rev3)
  ZS-042_RTC1 = ZS-042 RTC Module
  R1 = Resistor [tolerance=±1% resistance=10k package=THT]
  R2 = Resistor [tolerance=±1% resistance=150 package=THT]
  R3 = Resistor [tolerance=±1% resistance=150 package=THT]
  R4 = Resistor [tolerance=±1% resistance=120 package=THT]
  LED1 = RGB LED - (4 legs) [package="5 mm [THT]"]
  S2 = Pushbutton [package="[THT]"]
  S3 = Pushbutton [package="[THT]"]
  R5 = Resistor [tolerance=±1% resistance=10k package=THT]
  R6 = Resistor [tolerance=±1% resistance=10k package=THT]

nets:
  5V: S1.Pin_1, S1.Pin_2, Part2.5V, ZS-042_RTC1.VCC, LED1.common_anode, S2.Pin_1, S2.Pin_2, S3.Pin_1, S3.Pin_2
  N1: S1.Pin_3, S1.Pin_4, Part2.D2, R1.Pin_1
  N2: Part2.D8, S3.Pin_3, S3.Pin_4, R6.Pin_1
  N3: Part2.D9_PWM, R3.Pin_1
  N4: Part2.D10_PWM/SS, R2.Pin_1
  N5: Part2.D11_PWM/MOSI, R4.Pin_1
  N6: Part2.A4/SDA, ZS-042_RTC1.SDA
  N7: Part2.A5/SCL, ZS-042_RTC1.SCL
  N8: Part2.D7, S2.Pin_3, S2.Pin_4, R5.Pin_1
  GND: Part2.GND, ZS-042_RTC1.GND, R1.Pin_0, R5.Pin_0, R6.Pin_0
  N9: R2.Pin_0, LED1.green_cathode
  N10: R3.Pin_0, LED1.red_cathode
  N11: R4.Pin_0, LED1.blue_cathode

notes:
  Reset
  Record
  Fast forward
