# Fritzing sketch Reminder-led-Nano (saved by Fritzing 0.9.3b)
breadboards: 1

parts:
  S1 = Pushbutton [package="[THT]"]
  ZS-042_RTC1 = ZS-042 RTC Module
  R1 = Resistor [tolerance=±1% resistance=10k package=THT]
  R2 = Resistor [tolerance=±1% resistance=150 package=THT]
  R3 = Resistor [tolerance=±1% resistance=150 package=THT]
  R4 = Resistor [tolerance=±1% resistance=120 package=THT]
  LED1 = RGB LED - (4 legs) [package="5 mm [THT]"]  # not connected
  S2 = Pushbutton [package="[THT]"]
  S3 = Pushbutton [package="[THT]"]
  R5 = Resistor [tolerance=±1% resistance=10k package=THT]
  R6 = Resistor [tolerance=±1% resistance=10k package=THT]
  Part3 = Arduino Nano (Rev3.0)

nets:
  VCC: S1.Pin_1, S1.Pin_2, ZS-042_RTC1.VCC, S2.Pin_1, S2.Pin_2, S3.Pin_1, S3.Pin_2, Part3.5V
  N1: S1.Pin_3, S1.Pin_4, R1.Pin_1, Part3.D2
  GND: ZS-042_RTC1.GND, R1.Pin_0, R5.Pin_0, R6.Pin_0, Part3.GND
  N2: ZS-042_RTC1.SDA, Part3.A4
  N3: ZS-042_RTC1.SCL, Part3.A5
  N4: R2.Pin_1, Part3.D10
  N5: R3.Pin_1, Part3.D9
  N6: R4.Pin_1, Part3.D11/MOSI
  N7: S2.Pin_3, S2.Pin_4, R5.Pin_1, Part3.D8
  N8: S3.Pin_3, S3.Pin_4, R6.Pin_1, Part3.D7

notes:
  Reset
  Record
  Fast forward
